// Logisim project processor.circ as structural Verilog
module monocycle_processor (
);

  program_counter program_counter_1 ();  // open: enable, clock, reset, address
endmodule

module program_counter (
  input  enable,
  input  clock,
  input  reset,
  output [31:0] address
);

  wire [31:0] register_1_q;

  Register #(.width(32)) register_1 (.D(address), .en(enable), .clk(clock), .Q(register_1_q), .clr(reset));
  Adder #(.width(32)) adder_1 (.a(32'h4), .b(register_1_q), .out(address));  // open: cin, cout
endmodule
